# Fritzing sketch RSI2CHelloFromArduino (saved by Fritzing 0.7.3b)
breadboards: 1

parts:
  RSi2c_V1_Rev_1 = RSi2c v1 rev2 [part_number=RSI2CV1REV2]
  R1 = Resistor [tolerance=±5% resistance=220 package=THT]
  LED1 = LED - 5mm [color="Red (633nm)" package="5 mm [THT]"]
  Arduino1 = Arduino

nets:
  5V: RSi2c_V1_Rev_1.VCC#7, Arduino1.+5V
  N1: RSi2c_V1_Rev_1.SDA, Arduino1.A4
  N2: RSi2c_V1_Rev_1.SCL, Arduino1.A5
  N3: RSi2c_V1_Rev_1.P1, R1.Pin_0
  GND: RSi2c_V1_Rev_1.GND#18, LED1.cathode, Arduino1.GND
  N4: R1.Pin_1, LED1.anode

custom parts:
  RSi2c v1 rev2: Robotic Sequencing I2C intelligent module with upto 8 digital IO, 8 analog input, 3 pwm, 8 RC Servo and 1 step motor interface with linear acceleration profile using a simple commands set. Up to 127 module can be chained together.
